# Fritzing sketch push_button (saved by Fritzing 0.9.3b)
breadboards: 1

parts:
  LED1 = LED - 5mm [color="Red (633nm)" package="5 mm [THT]"]
  Raspberry_Pi_1 = Raspberry Pi 3 [part_number=RPI-3-V1.2]
  R1 = Resistor [tolerance=±5% resistance=330 package="0402 [SMD]"]
  S1 = Pushbutton [package="[SMD]"]

nets:
  N1: LED1.cathode, R1.Pin_0
  N2: LED1.anode, Raspberry_Pi_1.GPIO2
  N3: Raspberry_Pi_1.GIPO16, S1.Pin_2
  N4: Raspberry_Pi_1.GND, R1.Pin_1
  N5: Raspberry_Pi_1.5V, S1.Pin_3, S1.Pin_4

// code stored in the sketch: ledStrip.ino
#include "Adafruit_WS2801.h"
#include "SPI.h" // Comment out this line if using Trinket or Gemma
#ifdef __AVR_ATtiny85__
 #include <avr/power.h>
#endif
    #include <avr/sleep.h>  
     
/*****************************************************************************
Example sketch for driving Adafruit WS2801 pixels!


  Designed specifically to work with the Adafruit RGB Pixels!
  12mm Bullet shape ----> https://www.adafruit.com/products/322
  12mm Flat shape   ----> https://www.adafruit.com/products/738
  36mm Square shape ----> https://www.adafruit.com/products/683

  These pixels use SPI to transmit the color data, and have built in
  high speed PWM drivers for 24 bit color per pixel
  2 pins are required to interface

  Adafruit invests time and resources providing this open source code, 
  please support Adafruit and open-source hardware by purchasing 
  products from Adafruit!

  Written by Limor Fried/Ladyada for Adafruit Industries.  
  BSD license, all text above must be included in any redistribution

*****************************************************************************/

// Choose which 2 pins you will use for output.
// Can be any valid output pins.
// The colors of the wires may be totally different so
// BE SURE TO CHECK YOUR PIXELS TO SEE WHICH WIRES TO USE!
uint8_t dataPin  = 4;    // Yellow wire on Adafruit Pixels
uint8_t clockPin = 5;    // Green wire on Adafruit Pixels
int     wakePin = 2;                 // pin used for waking up  
int     sleepPin = 3;
int     led=13;  
   
// Don't forget to connect the ground wire to Arduino ground,
// and the +5V wire to a +5V supply

// Set the first variable to the NUMBER of pixels. 25 = 25 pixels in a row
Adafruit_WS2801 strip = Adafruit_WS2801(32, dataPin, clockPin);


void wakeUpNow() 
{  
}  
      
void sleepNow() 
{   
   set_sleep_mode(SLEEP_MODE_PWR_DOWN);   // sleep mode is set here  
   sleep_enable();          // enables the sleep bit in the mcucr register  
   attachInterrupt(0,wakeUpNow, LOW); // use interrupt 0 (pin 2) and run function  
   detachInterrupt(1);      // disables interrupt 0 on pin 2 so the wakeUpNow code will not be executed during normal running time.  
   sleep_mode();            // here the device is actually put to sleep!!  
   // THE PROGRAM CONTINUES FROM HERE AFTER WAKING UP  
   attachInterrupt(1,sleepNow, LOW); // use interrupt 0 (pin 2) and run function  
   detachInterrupt(0);      // disables interrupt 0 on pin 2 so the wakeUpNow code will not be executed during normal running time.  
   sleep_disable();         // first thing after waking from sleep: disable sleep...  
}  
       
void setup() {
   strip.begin();
   strip.show();
  
   pinMode(wakePin, INPUT_PULLUP);  
   pinMode(sleepPin, INPUT_PULLUP);   
      
   sleepNow();     // sleep function called here  
}
    
  

void loop() {
  // Some example procedures showing how to display to the pixels
  
  colorWipe(Color(255, 0, 0), 50);
  colorWipe(Color(0, 255, 0), 50);
  colorWipe(Color(0, 0, 255), 50);
  rainbow(20);
  rainbowCycle(20);
}

void rainbow(uint8_t wait) {
  int i, j;
   
  for (j=0; j < 256; j++) {     // 3 cycles of all 256 colors in the wheel
    for (i=0; i < strip.numPixels(); i++) {
      strip.setPixelColor(i, Wheel( (i + j) % 255));
    }  
    strip.show();   // write all the pixels out
    delay(wait);
  }
}

// Slightly different, this one makes the rainbow wheel equally distributed 
// along the chain
void rainbowCycle(uint8_t wait) {
  int i, j;
  
  for (j=0; j < 256 * 5; j++) {     // 5 cycles of all 25 colors in the wheel
    for (i=0; i < strip.numPixels(); i++) {
      // tricky math! we use each pixel as a fraction of the full 96-color wheel
      // (thats the i / strip.numPixels() part)
      // Then add in j which makes the colors go around per pixel
      // the % 96 is to make the wheel cycle around
      strip.setPixelColor(i, Wheel( ((i * 256 / strip.numPixels()) + j) % 256) );
    }  
    strip.show();   // write all the pixels out
    delay(wait);
  }
}

// fill the dots one after the other with said color
// good for testing purposes
void colorWipe(uint32_t c, uint8_t wait) {
  int i;
  
  for (i=0; i < strip.numPixels(); i++) {
      strip.setPixelColor(i, c);
      strip.show();
      delay(wait);
  }
}

/* Helper functions */

// Create a 24 bit color value from R,G,B
uint32_t Color(byte r, byte g, byte b)
{
  uint32_t c;
  c = r;
  c <<= 8;
  c |= g;
  c <<= 8;
  c |= b;
  return c;
}

//Input a value 0 to 255 to get a color value.
//The colours are a transition r - g -b - back to r
uint32_t Wheel(byte WheelPos)
{
  if (WheelPos < 85) {
   return Color(WheelPos * 3, 255 - WheelPos * 3, 0);
  } else if (WheelPos < 170) {
   WheelPos -= 85;
   return Color(255 - WheelPos * 3, 0, WheelPos * 3);
  } else {
   WheelPos -= 170; 
   return Color(0, WheelPos * 3, 255 - WheelPos * 3);
  }
}
